# Fritzing sketch maquette limiteur chauffage raspberry 2 platines (saved by Fritzing 0.9.1b)
breadboards: 2

parts:
  LED1 = smd LED [color="Red (633nm)" package="1206 [SMD]"]
  LED2 = RGB LED (com. anode, rbg) [package="5 mm [THT]"]
  R1 = Resistor [tolerance=±5% resistance=220 package="1206 [SMD]"]
  R2 = Resistor [tolerance=±5% resistance=220 package="1206 [SMD]"]
  R3 = Resistor [tolerance=±5% resistance=220 package="1206 [SMD]"]
  S1 = Pushbutton [package=THT]
  DHT11_Module1 = Humidity and Temperature Sensor DHT11
  C1 = Ceramic Capacitor [capacitance=100nF package="100 mil [THT, multilayer]"]
  Raspberry_Pi1 = Raspberry Pi B rev2

nets:
  N1: LED1.anode, Raspberry_Pi1.GND
  N2: LED2.red_cathode, R1.Pin_0
  N3: LED2.common_anode, S1.leg1, DHT11_Module1.GND, C1.0
  N4: LED2.blue_cathode, R2.Pin_0
  N5: LED2.green_cathode, R3.Pin_0
  N6: R1.Pin_1, Raspberry_Pi1.GPIO_22
  N7: R2.Pin_1, Raspberry_Pi1.GPIO_23
  N8: R3.Pin_1, Raspberry_Pi1.GPIO_24
  N9: S1.leg0, C1.1, Raspberry_Pi1.GPIO_2
  N10: DHT11_Module1.Data_Signal, Raspberry_Pi1.GPIO_4
  VCC: DHT11_Module1.Vcc, Raspberry_Pi1.3V3

custom parts:
  Humidity and Temperature Sensor DHT11: Digital relative humidity & temperature sensor DHT11 (on PCB)
